# Fritzing sketch schematics (saved by Fritzing 1.0.5)

parts:
  A3 = ESP32-S3-WROOM-1-N16R8 dev board
  Componente4 = LIPO-2200mAh
  Componente5 = DC-DC Power Module (5v)  # not connected
  Componente6 = DC-DC Power Module (5v)
  JP7 = Header 3 [package=screwterminal-3.5mm-3_lock.007s]  # not connected
  Componente7 = LIPO-2200mAh
  Componente8 = DC-DC Power Module (5v)
  Componente9 = DC-DC Power Module (5v)
  A4 = ESP32-S3-WROOM-1-N16R8 dev board
  J14 = Basic Servo
  J15 = Basic Servo
  J16 = Basic Servo
  J17 = Basic Servo
  Componente10 = LIPO-2200mAh
  Componente12 = DC-DC Power Module (5v)
  A5 = ESP32-S3-WROOM-1-N16R8 dev board
  M9 = BTS7960
  M10 = BTS7960
  M11 = DC Motor [voltage_(max)=6V voltage_(min)=3V]  # not connected
  M12 = DC Motor [voltage_(max)=6V voltage_(min)=3V]  # not connected
  M13 = DC Motor [voltage_(max)=6V voltage_(min)=3V]  # not connected
  M14 = DC Motor [voltage_(max)=6V voltage_(min)=3V]  # not connected
  M15 = DC Motor [voltage_(max)=6V voltage_(min)=3V]  # not connected
  M16 = DC Motor [voltage_(max)=6V voltage_(min)=3V]  # not connected
  Componente13 = LIPO-2200mAh
  M17 = DC Motor [voltage_(max)=6V voltage_(min)=3V]  # not connected
  M18 = DC Motor [voltage_(max)=6V voltage_(min)=3V]  # not connected
  M19 = DC Motor [voltage_(max)=6V voltage_(min)=3V]  # not connected
  M20 = DC Motor [voltage_(max)=6V voltage_(min)=3V]  # not connected
  M21 = BTS7960
  M22 = BTS7960
  Componente14 = DC-DC Power Module (5v)
  A6 = ESP32-S3-WROOM-1-N16R8 dev board
  M23 = DC Motor [voltage_(max)=6V voltage_(min)=3V]  # not connected
  M24 = DC Motor [voltage_(max)=6V voltage_(min)=3V]  # not connected
  J18 = Basic Servo
  J19 = Basic Servo
  J20 = Basic Servo
  Componente15 = DC-DC Power Module (5v)
  J21 = Basic Servo

nets:
  N1: A3.Pin_21, Componente6.Vout
  N2: Componente4.+, Componente6.Vin
  N3: Componente4.-, Componente6.GND
  N4: Componente7.+, Componente9.Vin
  N5: Componente7.-, Componente9.GND
  N6: Componente8.Vout, J14.vcc
  N7: Componente9.Vout, A4.Pin_21
  N8: A4.Pin_7, J17.pulse
  N9: A4.Pin_35, J16.pulse
  N10: A4.Pin_38, J14.pulse
  N11: A4.Pin_39, J15.pulse
  N12: Componente10.+, Componente12.Vin
  N13: Componente10.-, Componente12.GND
  N14: Componente12.Vout, A5.Pin_21
  N15: A5.Pin_16, M10.pin1
  N16: A5.Pin_17, M10.pin2
  N17: A5.Pin_18, M9.pin1
  N18: A5.Pin_19, M9.pin2
  N19: A5.Pin_22, A5.Pin_24, A5.Pin_44, M9.pin8
  N20: Componente13.+, Componente14.Vin
  N21: Componente13.-, Componente14.GND
  N22: M21.pin1, A6.Pin_16
  N23: M21.pin2, A6.Pin_17
  N24: M22.pin1, A6.Pin_18
  N25: M22.pin2, A6.Pin_19
  N26: M22.pin8, A6.Pin_22, A6.Pin_24, A6.Pin_44
  N27: Componente14.Vout, A6.Pin_21
  N28: A6.Pin_7, J18.pulse
  N29: A6.Pin_35, J19.pulse
  N30: A6.Pin_38, J21.pulse
  N31: A6.Pin_39, J20.pulse
  N32: Componente15.GND*, J21.gnd

notes:
  UBEC 5V/3A
  ESP32
  UBEC 6V/8A
  Servos
  12V for DC Motors
  Lipo 3s
  RF
  GPIO 38
  RB
  GPIO 7
  LB
  GPIO 42
  LF
  GPIO 41

custom parts:
  ESP32-S3-WROOM-1-N16R8 dev board: ESP32-S3 WIFI+BLE5.0 Development Board ESP32-S3-WROOM-1-N16R8(16M Flash/8SRAM).
  LIPO-2200mAh: 2200mAh Lipo-battery
  DC-DC Power Module (5v): DC-DC Power Module based con AMS1117-5.0 Input: DC 6~12V (input power must higher 1V than output power); Output: 5V (+/-0.05V error), 800mA
  BTS7960: BTS7960 43A Peak Power H-Bridge PWM Motor Driver
